// Logisim project s-mips.circ as structural Verilog: 28 circuits, main circuit Control Unit
module S_MIPS_Board (
  output halt
);

  wire button_1_out, CLK, CS, d_ff_1_q, R_W, Reset_out, RST, TTY_EN;
  wire [2:0] KDB;
  wire [3:0] Mask, ram_1_read_time, ram_1_write_time;
  wire [6:0] KDB_DATA, TTY_DATA;
  wire [15:0] Addr;
  wire [31:0] ram_1_data_out_0, ram_1_data_out_1, ram_1_data_out_2, ram_1_data_out_3, s_mips_1_ram_in_0,
       s_mips_1_ram_in_1, s_mips_1_ram_in_2, s_mips_1_ram_in_3;

  TTY #(.rows(25), .cols(80)) tty_1 (.data(TTY_DATA), .clk(CLK), .we(TTY_EN), .clr(RST));
  RAM ram_1 (
    .Address(Addr), .Data_Out_0(ram_1_data_out_0), .Data_Out_1(ram_1_data_out_1),
    .Data_Out_2(ram_1_data_out_2), .Data_Out_3(ram_1_data_out_3), .Data_In_0(s_mips_1_ram_in_0),
    .Data_In_1(s_mips_1_ram_in_1), .Data_In_2(s_mips_1_ram_in_2), .Data_In_3(s_mips_1_ram_in_3), .Mask(Mask),
    .nRead_Write(R_W), .Chip_Select(CS), .Read_Time(ram_1_read_time), .Reset(button_1_out),
    .Write_Time(ram_1_write_time));
  Button button_1 (.out(button_1_out));
  Keyboard #(.buflen(64)) keyboard_1 (.clk(CLK), .re(KDB[0]), .avail(KDB[2]), .data(KDB_DATA));  // open: clr
  S_MIPS s_mips_1 (
    .Kbd_Enable(KDB[0]), .Address(Addr), .Kbd_Clear(KDB[1]), .Kbd_Available(KDB[2]),
    .RAM_In_0(s_mips_1_ram_in_0), .Kbd_ASCII_Data(KDB_DATA), .RAM_In_1(s_mips_1_ram_in_1),
    .TTY_Enable(TTY_EN), .RAM_In_2(s_mips_1_ram_in_2), .RAM_In_3(s_mips_1_ram_in_3),
    .TTY_ASCII_Data(TTY_DATA), .Reset(RST), .RAM_Out_0(ram_1_data_out_0), .Clock(CLK),
    .RAM_Out_1(ram_1_data_out_1), .Stop(halt), .RAM_Out_2(ram_1_data_out_2), .RAM_Out_3(ram_1_data_out_3),
    .Mask(Mask), .Read_Time(ram_1_read_time), .Write_Time(ram_1_write_time), .nRead_Write(R_W),
    .Chip_Select(CS));
  D_Flip_Flop d_ff_1 (.clk(CLK), .D(1'b1), .Q(d_ff_1_q), .reset(Reset_out));  // open: Qn, preset, en
  Button Reset (.out(Reset_out));
  Clock clock_1 (.out(CLK));
  D_Flip_Flop d_ff_2 (.clk(CLK), .D(d_ff_1_q), .Qn(RST), .reset(Reset_out));  // open: Q, preset, en

  // Notes on the sheet:
  //   NO MODIFICAR
  //   Keyboard
endmodule

module RAM (
  input  [15:0] Address,
  input  [31:0] Data_In_0,
  input  [31:0] Data_In_1,
  input  [31:0] Data_In_2,
  input  [31:0] Data_In_3,
  input  [3:0] Mask,
  input  nRead_Write,
  input  Chip_Select,
  input  Reset,
  output [31:0] Data_Out_0,
  output [31:0] Data_Out_1,
  output [31:0] Data_Out_2,
  output [31:0] Data_Out_3,
  output [3:0] Read_Time,
  output [3:0] Write_Time
);

  wire and_2_out, and_3_out, and_4_out, and_5_out, and_6_out, and_7_out, and_8_out, and_9_out, Changed, CLK,
       comparator_2_eq, comparator_3_eq, comparator_4_eq, comparator_5_eq, comparator_6_eq, Count,
       demultiplexer_3_out0, Idle, Idle_q, Load, Load0, Load1, nand_1_out, or_1_out, or_2_out, or_3_out,
       or_4_out, or_5_out, or_6_out, or_7_out, or_8_out, or_9_out, or_10_out, Proc_q, Update_Mem, Zero_Time;
  wire [3:0] counter_1_q, multiplexer_1_out, subtractor_1_out;
  wire [31:0] register_1_q, register_2_q, register_3_q, register_4_q, register_5_q;

  // Probe on 4'b0011
  // Probe on 4'b0101
  Multiplexer #(.width(4), .enable("false")) multiplexer_1 (
    .in0(4'b0011), .in1(4'b0101), .out(multiplexer_1_out), .sel(nRead_Write));
  or or_1 (or_1_out, Idle, Update_Mem);
  or or_2 (or_2_out, ~Chip_Select, Reset);  // OR_Gate
  Subtractor #(.width(4)) subtractor_1 (.a(multiplexer_1_out), .b(4'b0010), .out(subtractor_1_out));  // open: bin, bout
  D_Flip_Flop u_Idle (.clk(CLK), .D(or_1_out), .Q(Idle_q), .preset(or_2_out));  // open: Qn, en, reset
  Demultiplexer #(.enable("false")) demultiplexer_1 (.out0(Idle), .out1(Load0), .in(Idle_q), .sel(Changed));
  // Probe on counter_1_q
  Counter #(.width(4), .max('hf)) counter_1 (
    .load(Load), .D(subtractor_1_out), .count(Count), .Q(counter_1_q), .clk(CLK), .clr(or_3_out));  // open: carry
  or or_3 (or_3_out, ~Chip_Select, Reset);  // OR_Gate
  Comparator #(.width(4), .mode("unsigned")) comparator_1 (
    .a(4'b0000), .b(counter_1_q), .eq(Zero_Time));  // open: gt, lt
  or or_4 (or_4_out, Count, Load0, Load1);
  Register #(.width(32)) register_1 (.D(Data_In_0), .en(Chip_Select), .Q(register_1_q), .clk(CLK), .clr(or_5_out));
  or or_5 (or_5_out, ~Chip_Select, Reset);  // OR_Gate
  Register #(.width(32)) register_2 (.D(Data_In_1), .en(Chip_Select), .Q(register_2_q), .clk(CLK), .clr(or_6_out));
  or or_6 (or_6_out, ~Chip_Select, Reset);  // OR_Gate
  Register #(.width(32)) register_3 (.D(Data_In_2), .en(Chip_Select), .Q(register_3_q), .clk(CLK), .clr(or_7_out));
  or or_7 (or_7_out, ~Chip_Select, Reset);  // OR_Gate
  Register #(.width(32)) register_4 (.D(Data_In_3), .en(Chip_Select), .Q(register_4_q), .clk(CLK), .clr(or_8_out));
  or or_8 (or_8_out, ~Chip_Select, Reset);  // OR_Gate
  Register #(.width(32)) register_5 (
    .D({{11{1'b1}}, nRead_Write, Mask, Address}), .en(Chip_Select), .Q(register_5_q), .clk(CLK),
    .clr(or_9_out));
  or or_9 (or_9_out, ~Chip_Select, Reset);  // OR_Gate
  D_Flip_Flop Proc (.clk(CLK), .D(or_4_out), .Q(Proc_q), .reset(or_10_out));  // open: Qn, preset, en
  or or_10 (or_10_out, ~Chip_Select, Reset);  // OR_Gate
  Demultiplexer #(.enable("false")) demultiplexer_2 (
    .out0(Count), .out1(Update_Mem), .in(demultiplexer_3_out0), .sel(Zero_Time));
  Demultiplexer #(.enable("false")) demultiplexer_3 (
    .out0(demultiplexer_3_out0), .out1(Load1), .in(Proc_q), .sel(Changed));
  Clock clock_1 (.out(CLK));
  Comparator #(.width(32)) comparator_2 (.a(register_1_q), .b(Data_In_0), .eq(comparator_2_eq));  // open: gt, lt
  Comparator #(.width(32)) comparator_3 (.a(register_2_q), .b(Data_In_1), .eq(comparator_3_eq));  // open: gt, lt
  Comparator #(.width(32)) comparator_4 (.a(register_3_q), .b(Data_In_2), .eq(comparator_4_eq));  // open: gt, lt
  Comparator #(.width(32)) comparator_5 (.a(register_4_q), .b(Data_In_3), .eq(comparator_5_eq));  // open: gt, lt
  Comparator #(.width(32)) comparator_6 (
    .a(register_5_q), .b({{11{1'b1}}, nRead_Write, Mask, Address}), .eq(comparator_6_eq));  // open: gt, lt
  nand nand_1 (nand_1_out, comparator_6_eq, comparator_2_eq, comparator_3_eq, comparator_4_eq, comparator_5_eq);
  and and_1 (Changed, nand_1_out, Chip_Select);
  or or_11 (Load, Count, Load1, Load0);
  and and_2 (and_2_out, Mask[0], Update_Mem, nRead_Write);
  and and_3 (and_3_out, Mask[1], Update_Mem, nRead_Write);
  and and_4 (and_4_out, Mask[2], Update_Mem, nRead_Write);
  and and_5 (and_5_out, Mask[3], Update_Mem, nRead_Write);
  RAM_part #(.addrWidth(16), .dataWidth(32), .bus("separate")) ram_1 (
    .addr(Address), .din(Data_In_0), .data(Data_Out_0), .str(and_2_out), .sel(Chip_Select), .clk(CLK),
    .ld(and_6_out), .clr(Reset));
  and and_6 (and_6_out, ~nRead_Write, Idle);  // AND_Gate
  RAM_part #(.addrWidth(16), .dataWidth(32), .bus("separate")) ram_2 (
    .addr(Address), .din(Data_In_1), .data(Data_Out_1), .str(and_3_out), .sel(Chip_Select), .clk(CLK),
    .ld(and_7_out), .clr(Reset));
  and and_7 (and_7_out, ~nRead_Write, Idle);  // AND_Gate
  RAM_part #(.addrWidth(16), .dataWidth(32), .bus("separate")) ram_3 (
    .addr(Address), .din(Data_In_2), .data(Data_Out_2), .str(and_4_out), .sel(Chip_Select), .clk(CLK),
    .ld(and_8_out), .clr(Reset));
  and and_8 (and_8_out, ~nRead_Write, Idle);  // AND_Gate
  RAM_part #(.addrWidth(16), .dataWidth(32), .bus("separate")) ram_4 (
    .addr(Address), .din(Data_In_3), .data(Data_Out_3), .str(and_5_out), .sel(Chip_Select), .clk(CLK),
    .ld(and_9_out), .clr(Reset));
  and and_9 (and_9_out, ~nRead_Write, Idle);  // AND_Gate

  assign Read_Time = 4'b0011;
  assign Write_Time = 4'b0101;

  // Other names for the same wires on the sheet: M0 = Mask[0]; M1 = Mask[1]; M2 = Mask[2]; M3 = Mask[3];
  //   RW = nRead_Write; CLR = Reset; CS = Chip_Select; Load2 = Count

  // Notes on the sheet:
  //   NO MODIFICAR
  //   excepto quizás los valores RT y WT
  //   BANK0
  //   BANK1
  //   BANK2
  //   BANK3
endmodule

module S_MIPS (
  input  Kbd_Available,
  input  [6:0] Kbd_ASCII_Data,
  input  [31:0] RAM_Out_0,
  input  [31:0] RAM_Out_1,
  input  Reset,
  input  [31:0] RAM_Out_2,
  input  Clock,
  input  [31:0] RAM_Out_3,
  input  [3:0] Read_Time,
  input  [3:0] Write_Time,
  output Kbd_Enable,
  output [15:0] Address,
  output Kbd_Clear,
  output TTY_Enable,
  output [6:0] TTY_ASCII_Data,
  output Stop,
  output [31:0] RAM_In_0,
  output [31:0] RAM_In_1,
  output [31:0] RAM_In_2,
  output [31:0] RAM_In_3,
  output [3:0] Mask,
  output nRead_Write,
  output Chip_Select
);

  wire ADD, ADDI, ALU, AND, and_2_out, and_3_out, and_4_out, ANDI, BEQ, BGTZ, BLEZ, BLTZ, BNE,
       branch_control_1_loadpc, CLRIF, CLRPC, CLRRF, CS_R, CS_W, d_ff_1_q, d_ff_2_q, DIV, DIVU, END_Fetch1,
       END_Fetch2, END_MODE2, END_W, EPop, EPush, ER, HALT, HI_LO, II, INME, IR, J, JR, KBD, LINST, LPC,
       LRAN, LW, MFHI, MFLO, MUL, MULU, NOP, NOR, OR, or_2_out, or_3_out, or_4_out, or_5_out, or_6_out,
       or_10_out, or_16_out, ORI, POP, PUSH, R_RAM, R_W, Register, RND, RW_HI_LO, S, SLT, SLTI, SLTIU, SLTU,
       START_FETCH2, START_MODE1, START_MODE2, SUB, SW, TTY, W_RAM, XOR, XORI;
  wire [2:0] selector_input_1_out_8;
  wire [4:0] OP_A, OP_B, RD, SAVE;
  wire [5:0] Code;
  wire [7:0] read_ram_1_out_15, read_ram_1_out_15_2, read_ram_1_out_15_3, read_ram_1_out_15_4;
  wire [15:0] I015, Read_A, Write_A;
  wire [25:0] Address_t;
  wire [31:0] _4, A, adder_2_out, ALU_RESULT, B, branch_control_1_out_13, Data_to_Save, DLW, HI, I32, INPUT,
       Instruction, Kbd_Rd, LO, mux_1x32_1_o, mux_1x32_2_o, mux_1x32_4_o, mux_1x32_5_o, mux_1x32_6_o, PC_OUT,
       R_INME, random_1_out, register_1_q, register_2_q, RHI, RLO, SP;

  // Probe on R_INME
  Random #(.width(32)) random_1 (.clk(Clock), .next(LRAN), .out(random_1_out));  // open: clr
  assign I32 = {{16{I015[15]}}, I015};  // Bit_Extender bit_extender_1
  // Probe on ALU_RESULT
  MUX_3x32 mux_3x32_1 (
    .I0(ALU_RESULT), .I1(R_INME), .I2(Data_to_Save), .I3(HI), .I4(LO), .I5(random_1_out), .I6(Kbd_Rd),
    .in_9(selector_input_1_out_8), .out_10(INPUT));  // open: I7
  Selector_Input selector_input_1 (
    .ALU(ALU), .INM(INME), .DS(R_RAM), .HI(MFHI), .LO(MFLO), .RND(RND), .KBD(KBD),
    .out_8(selector_input_1_out_8));
  Adder #(.width(32)) adder_1 (.a(A), .b(I32), .out(DLW));  // open: cin, cout
  // Probe on INPUT
  MUX_1x32 mux_1x32_1 (.I1(SP), .O(mux_1x32_1_o), .I0(DLW), .in_3(POP));
  Multiplexer #(.width(16), .enable("false")) multiplexer_1 (
    .in0(Read_A), .in1(Write_A), .out(Address), .sel(nRead_Write));
  MUX_1x32 mux_1x32_2 (.I1(PC_OUT), .O(mux_1x32_2_o), .I0(mux_1x32_1_o), .in_3(START_MODE1));
  // Probe on OP_A
  D_Flip_Flop d_ff_1 (.clk(Clock), .D(HALT), .Q(d_ff_1_q), .en(1'b1), .reset(Reset));  // open: Qn, preset
  // Probe on INPUT
  or or_1 (ER, START_MODE1, START_MODE2);
  and and_1 (START_MODE2, START_FETCH2, or_2_out);
  Register #(.width(32)) register_1 (.D(A), .en(TTY), .Q(register_1_q), .clk(Clock), .clr(Reset));
  Read_Ram read_ram_1 (
    .RAMO0(RAM_Out_0), .RAMO1(RAM_Out_1), .I(mux_1x32_2_o), .RT(Read_Time), .in_5(START_MODE1),
    .RAMO2(RAM_Out_2), .RAMO3(RAM_Out_3), .CLK(Clock), .in_9(START_MODE2), .Reset(Reset), .EW(ER),
    .END_Mode1(END_Fetch1), .ADDR(Read_A), .out_14(CS_R),
    .out_15({read_ram_1_out_15, read_ram_1_out_15_2, read_ram_1_out_15_3, read_ram_1_out_15_4}),
    .END_Mode2(END_MODE2));
  or or_2 (or_2_out, POP, LW);
  or or_3 (or_3_out, EPop, EPush);
  Adder #(.width(32)) adder_2 (.a(SP), .b(_4), .out(adder_2_out));  // open: cin, cout
  Multiplexer #(.width(7), .enable("false")) multiplexer_2 (
    .in0({7{1'b0}}), .in1(register_1_q[6:0]), .out(TTY_ASCII_Data), .sel(TTY_Enable));
  Control_Unit control_unit_1 (
    .in_1(1'b1), .in_2(Reset), .in_3(Clock), .in_4(END_Fetch1), .in_5(PUSH), .in_6(R_RAM), .in_7(W_RAM),
    .in_8(END_Fetch2), .in_9(R_W), .in_10(RW_HI_LO), .in_11(KBD), .in_12(TTY), .in_13(d_ff_1_q),
    .out_14(CLRRF), .out_15(CLRPC), .out_16(Kbd_Clear), .out_17(CLRIF), .out_18(START_MODE1), .out_19(LRAN),
    .out_20(LINST), .out_21(EPush), .out_22(START_FETCH2), .out_23(Register), .out_24(HI_LO),
    .out_25(Kbd_Enable), .out_26(LPC), .out_27(Stop));
  Branch_Control branch_control_1 (
    .in_1(A), .in_2(B), .in_3(I015), .in_4(Address_t), .in_5(PC_OUT), .in_6(BNE), .in_7(J), .in_8(BEQ),
    .in_9(JR), .in_10(BLTZ), .in_11(BGTZ), .in_12(BLEZ), .LoadPC(branch_control_1_loadpc),
    .out_13(branch_control_1_out_13));
  Register_File register_file_1 (
    .in_2(INPUT), .in_3(OP_A), .in_5(OP_B), .in_6(R_W), .in_7(SAVE), .in_8(HI_LO), .IHI(RHI), .ILO(RLO),
    .ISP(adder_2_out), .SA(A), .SB(B), .OHI(HI), .OLO(LO), .OSP(SP), .in_11(or_3_out), .in_1(Clock),
    .in_4(CLRRF));
  PC pc_1 (.PC_Input(branch_control_1_out_13), .Enable(or_4_out), .PC_Output(PC_OUT), .Reset(CLRPC), .CLOK(Clock));
  or or_4 (or_4_out, branch_control_1_loadpc, LPC);
  // Probe on {read_ram_1_out_15_4, read_ram_1_out_15_3, read_ram_1_out_15_2, read_ram_1_out_15}
  Demultiplexer #(.width(32), .enable("false")) demultiplexer_1 (
    .out0(Data_to_Save), .out1(Instruction),
    .in({read_ram_1_out_15_4, read_ram_1_out_15_3, read_ram_1_out_15_2, read_ram_1_out_15}), .sel(START_MODE1));
  and and_2 (and_2_out, ~W_RAM, ~R_RAM);  // AND_Gate
  and and_3 (and_3_out, ~or_5_out, or_6_out);  // AND_Gate
  or or_5 (or_5_out, END_MODE2, END_W);
  and and_4 (and_4_out, END_Fetch2, EPop);
  MUX_1x32 mux_1x32_3 (.I1(32'h4), .O(_4), .I0(32'hfffffffc), .in_3(and_4_out));
  MUX_1x32 mux_1x32_4 (.I1(register_2_q), .O(mux_1x32_4_o), .I0(32'hfc000000), .in_3(d_ff_2_q));
  Register #(.width(32)) register_2 (.D(Instruction), .en(and_2_out), .Q(register_2_q), .clk(Clock), .clr(Reset));
  D_Flip_Flop d_ff_2 (.clk(Clock), .D(and_3_out), .Q(d_ff_2_q), .en(1'b1), .reset(Reset));  // open: Qn, preset
  or or_6 (or_6_out, W_RAM, R_RAM, END_Fetch1);
  Multiplexer #(.width(32), .enable("false")) multiplexer_3 (
    .in0({32{1'b1}}), .in1({{25{1'b0}}, Kbd_ASCII_Data}), .out(Kbd_Rd), .sel(Kbd_Available));
  MUX_1x32 mux_1x32_5 (.I1(B), .O(mux_1x32_5_o), .I0(A), .in_3(SW));
  // Probe on mux_1x32_5_o
  MUX_1x32 mux_1x32_6 (.I1(DLW), .O(mux_1x32_6_o), .I0(SP), .in_3(SW));
  Inmediate_I inmediate_i_1 (.in_1(I015), .out_4(R_INME), .in_2(Code), .in_3(A));
  or or_7 (END_Fetch2, END_MODE2, END_W);
  Instructions_Decoder instructions_decoder_1 (
    .INS(mux_1x32_4_o), .ADDI(ADDI), .ORI(ORI), .BEQ(BEQ), .SLTI(SLTI), .XORI(XORI), .BNE(BNE), .BLTZ(BLTZ),
    .SLTIU(SLTIU), .LW(LW), .BLEZ(BLEZ), .ANDI(ANDI), .SW(SW), .BGTZ(BGTZ), .II(II), .out_16(OP_A), .S(S),
    .NOP(NOP), .out_19(OP_B), .MULU(MULU), .IR(IR), .out_22(I015), .Address(Address_t), .SLTU(SLTU),
    .XOR(XOR), .out_26(RD), .Code(Code), .ADD(ADD), .DIV(DIV), .IJ(J), .AND(AND), .POP(POP), .RND(RND),
    .SUB(SUB), .DIVU(DIVU), .OR(OR), .PUSH(PUSH), .KBD(KBD), .MUL(MUL), .SLT(SLT), .NOR(NOR), .JR(JR),
    .MFHI(MFHI), .MFLO(MFLO), .HALT(HALT), .TTY(TTY));
  ALU alu_1 (
    .in_1(A), .in_2(Code), .in_3(B), .in_4(S), .out_7(RHI), .out_6(RLO), .out_5(ALU_RESULT));  // open: out_8, out_9, out_10, out_11, out_12
  or or_8 (R_RAM, LW, POP);
  or or_9 (W_RAM, SW, PUSH);
  Write_RAM write_ram_1 (
    .WT(Write_Time), .in_2(mux_1x32_6_o),
    .InputValue({mux_1x32_5_o[7:0], mux_1x32_5_o[15:8], mux_1x32_5_o[23:16], mux_1x32_5_o[31:24]}),
    .CLK(Clock), .Reset(Reset), .in_6(nRead_Write), .Mask(Mask), .out_8(Write_A), .out_9(CS_W),
    .out_10(RAM_In_0), .out_11(RAM_In_1), .out_12(RAM_In_2), .out_13(RAM_In_3), .out_14(END_W));
  and and_5 (nRead_Write, START_FETCH2, or_10_out);
  or or_10 (or_10_out, SW, PUSH);
  D_Flip_Flop d_ff_3 (.clk(Clock), .D(TTY), .Q(TTY_Enable), .reset(Reset));  // open: Qn, preset, en
  or or_11 (Chip_Select, CS_W, CS_R);
  or or_12 (R_RAM, POP, LW);
  or or_13 (W_RAM, SW, PUSH);
  or or_14 (RW_HI_LO, MUL, MULU, DIV, DIVU);
  or or_15 (INME, ANDI, ADDI, ORI, SLTIU, SLTI, XORI);
  or or_16 (or_16_out, LW, INME);
  Multiplexer #(.width(5), .enable("false")) multiplexer_4 (.in0(RD), .in1(OP_B), .out(SAVE), .sel(or_16_out));
  and and_6 (EPop, END_MODE2, POP);
  or or_17 (R_W, LW, ANDI, SUB, SLT, SLTU, AND, OR, MFHI, XORI, MFLO, SLTI, XOR, SLTIU, ORI, ADDI, NOR, KBD, ADD, RND, POP);
  or or_18 (ALU, SUB, ADD, SLT, SLTU, AND, OR, NOR, XOR);

  // Other names for the same wires on the sheet: KBD_DATA[6:0] = Kbd_ASCII_Data; CLK = Clock; CLR = Reset;
  //   CS = Chip_Select; K[15:0] = I015; I15 = I015[15]; KBD_AVAIL = Kbd_Available; KBD_CLR = Kbd_Clear; RAM = R_RAM;
  //   RAM_A[15:0] = Address; RAM_INPUT_0[31:0] = RAM_In_0; RAM_INPUT_1[31:0] = RAM_In_1; RAM_INPUT_2[31:0] = RAM_In_2;
  //   RAM_INPUT_3[31:0] = RAM_In_3; RAM_MASK[3:0] = Mask; RAM_OUTPUT_0[31:0] = RAM_Out_0;
  //   RAM_OUTPUT_1[31:0] = RAM_Out_1; RAM_OUTPUT_2[31:0] = RAM_Out_2; RAM_OUTPUT_3[31:0] = RAM_Out_3; RS[4:0] = OP_A;
  //   RT[4:0] = OP_B; EW = nRead_Write; RW = nRead_Write; TTY_DATA[6:0] = TTY_ASCII_Data

  // Notes on the sheet:
  //   RAM ADDRESS
  //   DATA FROM RAM
  //   DATA TO RAM
  //   DATA WRITE MASK
  //   RAM TIMING
  //   RAM CONTROL
  //   KEYBOARD
  //   TTY
  //   SEQUENCING
endmodule

// MUX
module MUX_1x32 (
  input  [31:0] I1,
  input  [31:0] I0,
  input  in_3,
  output [31:0] O
);

  wire I0_t, I1_t;

  Decoder #(.enable("false")) decoder_1 (.out0(I0_t), .out1(I1_t), .sel(in_3));
  assign O = I0_t ? I0 : 32'bz;  // Controlled_Buffer controlled_buffer_1
  assign O = I1_t ? I1 : 32'bz;  // Controlled_Buffer controlled_buffer_2

  // Other names for the same wires on the sheet: Out[31:0] = O; Selector = in_3
endmodule

// MUX
module MUX_2x32 (
  input  [31:0] I0,
  input  [31:0] I1,
  input  [31:0] I2,
  input  [31:0] I3,
  input  [1:0] in_5,
  output [31:0] out_6
);

  wire I0_t, I1_t, I2_t, I3_t;

  assign out_6 = I0_t ? I0 : 32'bz;  // Controlled_Buffer controlled_buffer_1
  Decoder #(.select(2), .enable("false")) decoder_1 (.out0(I0_t), .out1(I1_t), .out2(I2_t), .out3(I3_t), .sel(in_5));
  assign out_6 = I1_t ? I1 : 32'bz;  // Controlled_Buffer controlled_buffer_2
  assign out_6 = I2_t ? I2 : 32'bz;  // Controlled_Buffer controlled_buffer_3
  assign out_6 = I3_t ? I3 : 32'bz;  // Controlled_Buffer controlled_buffer_4

  // Other names for the same wires on the sheet: OUT[31:0] = out_6; Selector[1:0] = in_5
endmodule

// MUX
module MUX_3x32 (
  input  [31:0] I0,
  input  [31:0] I1,
  input  [31:0] I2,
  input  [31:0] I3,
  input  [31:0] I4,
  input  [31:0] I5,
  input  [31:0] I6,
  input  [31:0] I7,
  input  [2:0] in_9,
  output [31:0] out_10
);

  wire I0_t, I1_t, I2_t, I3_t, I4_t, I5_t, I6_t, I7_t;

  assign out_10 = I0_t ? I0 : 32'bz;  // Controlled_Buffer controlled_buffer_1
  assign out_10 = I1_t ? I1 : 32'bz;  // Controlled_Buffer controlled_buffer_2
  Decoder #(.select(3), .enable("false")) decoder_1 (
    .out0(I0_t), .out1(I1_t), .out2(I2_t), .out3(I3_t), .out4(I4_t), .out5(I5_t), .out6(I6_t), .out7(I7_t),
    .sel(in_9));
  assign out_10 = I2_t ? I2 : 32'bz;  // Controlled_Buffer controlled_buffer_3
  assign out_10 = I3_t ? I3 : 32'bz;  // Controlled_Buffer controlled_buffer_4
  assign out_10 = I4_t ? I4 : 32'bz;  // Controlled_Buffer controlled_buffer_5
  assign out_10 = I5_t ? I5 : 32'bz;  // Controlled_Buffer controlled_buffer_6
  assign out_10 = I6_t ? I6 : 32'bz;  // Controlled_Buffer controlled_buffer_7
  assign out_10 = I7_t ? I7 : 32'bz;  // Controlled_Buffer controlled_buffer_8

  // Other names for the same wires on the sheet: Out[31:0] = out_10; Selector[2:0] = in_9
endmodule

module MUX_4x32 (
  input  [31:0] I0,
  input  [31:0] I1,
  input  [31:0] I2,
  input  [31:0] I3,
  input  [31:0] I4,
  input  [31:0] I5,
  input  [31:0] I6,
  input  [31:0] I7,
  input  [31:0] I8,
  input  [31:0] I9,
  input  [31:0] I10,
  input  [31:0] I11,
  input  [31:0] I12,
  input  [31:0] I13,
  input  [31:0] I14,
  input  [31:0] I15,
  input  [3:0] in_17,
  output [31:0] out_18
);

  wire I0_t, I1_t, I2_t, I3_t, I4_t, I5_t, I6_t, I7_t, I8_t, I9_t, I10_t, I11_t, I12_t, I13_t, I14_t, I15_t;

  assign out_18 = I0_t ? I0 : 32'bz;  // Controlled_Buffer controlled_buffer_1
  assign out_18 = I8_t ? I8 : 32'bz;  // Controlled_Buffer controlled_buffer_2
  Decoder #(.select(4), .enable("false")) decoder_1 (
    .out0(I0_t), .out1(I1_t), .out2(I2_t), .out3(I3_t), .out4(I4_t), .out5(I5_t), .out6(I6_t), .out7(I7_t),
    .out8(I8_t), .out9(I9_t), .out10(I10_t), .out11(I11_t), .out12(I12_t), .out13(I13_t), .out14(I14_t),
    .out15(I15_t), .sel(in_17));
  assign out_18 = I1_t ? I1 : 32'bz;  // Controlled_Buffer controlled_buffer_3
  assign out_18 = I9_t ? I9 : 32'bz;  // Controlled_Buffer controlled_buffer_4
  assign out_18 = I2_t ? I2 : 32'bz;  // Controlled_Buffer controlled_buffer_5
  assign out_18 = I10_t ? I10 : 32'bz;  // Controlled_Buffer controlled_buffer_6
  assign out_18 = I3_t ? I3 : 32'bz;  // Controlled_Buffer controlled_buffer_7
  assign out_18 = I11_t ? I11 : 32'bz;  // Controlled_Buffer controlled_buffer_8
  assign out_18 = I4_t ? I4 : 32'bz;  // Controlled_Buffer controlled_buffer_9
  assign out_18 = I12_t ? I12 : 32'bz;  // Controlled_Buffer controlled_buffer_10
  assign out_18 = I5_t ? I5 : 32'bz;  // Controlled_Buffer controlled_buffer_11
  assign out_18 = I13_t ? I13 : 32'bz;  // Controlled_Buffer controlled_buffer_12
  assign out_18 = I6_t ? I6 : 32'bz;  // Controlled_Buffer controlled_buffer_13
  assign out_18 = I14_t ? I14 : 32'bz;  // Controlled_Buffer controlled_buffer_14
  assign out_18 = I7_t ? I7 : 32'bz;  // Controlled_Buffer controlled_buffer_15
  assign out_18 = I15_t ? I15 : 32'bz;  // Controlled_Buffer controlled_buffer_16

  // Other names for the same wires on the sheet: O[31:0] = out_18; Selector[3:0] = in_17
endmodule

// MUX
module MUL_5x32 (
  input  [31:0] I0,
  input  [31:0] I1,
  input  [31:0] I2,
  input  [31:0] I3,
  input  [31:0] I4,
  input  [31:0] I5,
  input  [31:0] I6,
  input  [31:0] I7,
  input  [31:0] I8,
  input  [31:0] I9,
  input  [31:0] I10,
  input  [31:0] I11,
  input  [31:0] I12,
  input  [31:0] I13,
  input  [31:0] I14,
  input  [31:0] I15,
  input  [31:0] I16,
  input  [31:0] I17,
  input  [31:0] I18,
  input  [31:0] I19,
  input  [31:0] I20,
  input  [31:0] I21,
  input  [31:0] I22,
  input  [31:0] I23,
  input  [31:0] I24,
  input  [31:0] I25,
  input  [31:0] I26,
  input  [31:0] I27,
  input  [31:0] I28,
  input  [31:0] I29,
  input  [31:0] I30,
  input  [31:0] I31,
  input  [4:0] in_33,
  output [31:0] out_34
);

  wire I0_t, I1_t, I2_t, I3_t, I4_t, I5_t, I6_t, I7_t, I8_t, I9_t, I10_t, I11_t, I12_t, I13_t, I14_t, I15_t,
       I16_t, I17_t, I18_t, I19_t, I20_t, I21_t, I22_t, I23_t, I24_t, I25_t, I26_t, I27_t, I28_t, I29_t,
       I30_t, I31_t;

  assign out_34 = I0_t ? I0 : 32'bz;  // Controlled_Buffer controlled_buffer_1
  assign out_34 = I8_t ? I8 : 32'bz;  // Controlled_Buffer controlled_buffer_2
  assign out_34 = I16_t ? I16 : 32'bz;  // Controlled_Buffer controlled_buffer_3
  assign out_34 = I24_t ? I24 : 32'bz;  // Controlled_Buffer controlled_buffer_4
  assign out_34 = I1_t ? I1 : 32'bz;  // Controlled_Buffer controlled_buffer_5
  assign out_34 = I9_t ? I9 : 32'bz;  // Controlled_Buffer controlled_buffer_6
  assign out_34 = I17_t ? I17 : 32'bz;  // Controlled_Buffer controlled_buffer_7
  assign out_34 = I25_t ? I25 : 32'bz;  // Controlled_Buffer controlled_buffer_8
  Decoder #(.select(5), .enable("false")) decoder_1 (
    .out0(I0_t), .out1(I1_t), .out2(I2_t), .out3(I3_t), .out4(I4_t), .out5(I5_t), .out6(I6_t), .out7(I7_t),
    .out8(I8_t), .out9(I9_t), .out10(I10_t), .out11(I11_t), .out12(I12_t), .out13(I13_t), .out14(I14_t),
    .out15(I15_t), .out16(I16_t), .out17(I17_t), .out18(I18_t), .out19(I19_t), .out20(I20_t), .out21(I21_t),
    .out22(I22_t), .out23(I23_t), .out24(I24_t), .out25(I25_t), .out26(I26_t), .out27(I27_t), .out28(I28_t),
    .out29(I29_t), .out30(I30_t), .out31(I31_t), .sel(in_33));
  assign out_34 = I2_t ? I2 : 32'bz;  // Controlled_Buffer controlled_buffer_9
  assign out_34 = I10_t ? I10 : 32'bz;  // Controlled_Buffer controlled_buffer_10
  assign out_34 = I18_t ? I18 : 32'bz;  // Controlled_Buffer controlled_buffer_11
  assign out_34 = I26_t ? I26 : 32'bz;  // Controlled_Buffer controlled_buffer_12
  assign out_34 = I3_t ? I3 : 32'bz;  // Controlled_Buffer controlled_buffer_13
  assign out_34 = I11_t ? I11 : 32'bz;  // Controlled_Buffer controlled_buffer_14
  assign out_34 = I19_t ? I19 : 32'bz;  // Controlled_Buffer controlled_buffer_15
  assign out_34 = I27_t ? I27 : 32'bz;  // Controlled_Buffer controlled_buffer_16
  assign out_34 = I4_t ? I4 : 32'bz;  // Controlled_Buffer controlled_buffer_17
  assign out_34 = I12_t ? I12 : 32'bz;  // Controlled_Buffer controlled_buffer_18
  assign out_34 = I20_t ? I20 : 32'bz;  // Controlled_Buffer controlled_buffer_19
  assign out_34 = I28_t ? I28 : 32'bz;  // Controlled_Buffer controlled_buffer_20
  assign out_34 = I5_t ? I5 : 32'bz;  // Controlled_Buffer controlled_buffer_21
  assign out_34 = I13_t ? I13 : 32'bz;  // Controlled_Buffer controlled_buffer_22
  assign out_34 = I21_t ? I21 : 32'bz;  // Controlled_Buffer controlled_buffer_23
  assign out_34 = I29_t ? I29 : 32'bz;  // Controlled_Buffer controlled_buffer_24
  assign out_34 = I6_t ? I6 : 32'bz;  // Controlled_Buffer controlled_buffer_25
  assign out_34 = I14_t ? I14 : 32'bz;  // Controlled_Buffer controlled_buffer_26
  assign out_34 = I22_t ? I22 : 32'bz;  // Controlled_Buffer controlled_buffer_27
  assign out_34 = I30_t ? I30 : 32'bz;  // Controlled_Buffer controlled_buffer_28
  assign out_34 = I7_t ? I7 : 32'bz;  // Controlled_Buffer controlled_buffer_29
  assign out_34 = I15_t ? I15 : 32'bz;  // Controlled_Buffer controlled_buffer_30
  assign out_34 = I23_t ? I23 : 32'bz;  // Controlled_Buffer controlled_buffer_31
  assign out_34 = I31_t ? I31 : 32'bz;  // Controlled_Buffer controlled_buffer_32

  // Other names for the same wires on the sheet: O[31:0] = out_34; selector[4:0] = in_33
endmodule

module ALU (
  input  [31:0] in_1,
  input  [5:0] in_2,
  input  [31:0] in_3,
  input  in_4,
  output [31:0] out_5,
  output [31:0] out_6,
  output [31:0] out_7,
  output out_8,
  output out_9,
  output out_10,
  output out_11,
  output out_12
);

  wire ADD, and_5_out, and_6_out, and_7_out, CADD, comparator_2_eq, comparer_1_out_5, CSUB, MD, not_2_out,
       not_3_out, not_4_out, not_5_out, not_6_out, not_7_out, not_8_out, not_9_out, SIGN, SUB;
  wire [3:0] bitadder_1_out;
  wire [30:0] Op;
  wire [31:0] HID, HIM, LoD, LoM, RADD, RAND, RNOR, ROR, RSLT, RSUB, RXOR;

  MUX_1x32 mux_1x32_1 (.I1(HID), .O(out_7), .I0(HIM), .in_3(in_2[1]));
  MUX_1x32 mux_1x32_2 (.I1(out_5), .O({out_11, Op}), .I0(out_6), .in_3(in_2[5]));
  not not_1 (SIGN, in_2[0]);
  Comparator #(.width(32)) comparator_1 (.a({out_11, Op}), .b({32{1'b0}}), .eq(out_9), .lt(out_8));  // open: gt
  MUX_1x32 mux_1x32_3 (.I1(LoD), .O(out_6), .I0(LoM), .in_3(in_2[1]));
  Adder #(.width(32)) adder_1 (.a(in_1), .b(in_3), .out(RADD), .cout(CADD));  // open: cin
  Subtractor #(.width(32)) subtractor_1 (.a(in_1), .b(in_3), .out(RSUB), .bout(CSUB));  // open: bin
  MUL mul_1 (.in_1(in_1), .in_2(in_3), .in_3(SIGN), .HIGHT(HIM), .LOW(LoM));
  DIV div_1 (.Dividend(in_1), .Divisor(in_3), .in_3(SIGN), .Output(LoD), .Remainder(HID));
  Comparer comparer_1 (.A(in_1), .B(in_3), .in_3(SIGN), .out_5(comparer_1_out_5));  // open: out_4, out_6
  assign RAND = in_1 & in_3;  // AND_Gate and_1, 32 bits wide
  assign ROR = in_1 | in_3;  // OR_Gate or_1, 32 bits wide
  assign RXOR = in_1 ^ in_3;  // XOR_Gate xor_1, 32 bits wide
  BitAdder bitadder_1 (.in0(Op[7:0]), .out(bitadder_1_out));
  not not_2 (not_2_out, in_2[4]);
  not not_3 (not_3_out, in_2[3]);
  not not_4 (not_4_out, in_2[2]);
  not not_5 (not_5_out, in_2[1]);
  not not_6 (not_6_out, in_2[4]);
  not not_7 (not_7_out, in_2[3]);
  not not_8 (not_8_out, in_2[2]);
  not not_9 (not_9_out, in_2[2]);
  assign RSLT = {{31{1'b0}}, comparer_1_out_5};  // Bit_Extender bit_extender_1
  assign RNOR = ~ROR;  // NOT_Gate not_10, 32 bits wide
  not not_11 (out_10, bitadder_1_out[0]);
  and and_2 (ADD, not_2_out, not_3_out, not_4_out, not_5_out);
  and and_3 (SUB, not_6_out, not_7_out, not_8_out, in_2[1]);
  and and_4 (MD, in_2[4], in_2[3], not_9_out);
  and and_5 (and_5_out, ADD, CADD);
  and and_6 (and_6_out, SUB, CSUB);
  and and_7 (and_7_out, MD, comparator_2_eq);
  Comparator #(.width(32)) comparator_2 (.a(out_6), .b({32{1'b0}}), .eq(comparator_2_eq));  // open: gt, lt
  MUX_4x32 mux_4x32_1 (
    .I0(RADD), .I2(RSUB), .I4(RAND), .I5(ROR), .I7(RNOR), .I8(RXOR), .I10(RSLT), .I11(RSLT),
    .in_17(in_2[3:0]), .out_18(out_5));  // open: I1, I3, I6, I9, I12, I13, I14, I15
  or or_2 (out_12, and_5_out, and_6_out, and_7_out);

  // Other names for the same wires on the sheet: A[31:0] = in_1; B[31:0] = in_3; CF = out_12; Hi[31:0] = out_7;
  //   Lo[31:0] = out_6; NF = out_8; Op[31] = out_11; SF = out_11; Op___Code[5:0] = in_2; _1 = in_2[1]; _2 = in_2[2];
  //   _3 = in_2[3]; _4 = in_2[4]; Lo_R = in_2[5]; PF = out_10; R[31:0] = out_5; S = in_4; ZF = out_9

  // Notes on the sheet:
  //   Inputs
  //   OUTPUTS
  //   Operation
  //   FLAGS
endmodule

module MUL (
  input  [31:0] in_1,
  input  [31:0] in_2,
  input  in_3,
  output [31:0] HIGHT,
  output [31:0] LOW
);

  wire and_1_out, C1, C2, C3;
  wire [1:0] C_U;
  wire [29:0] O;
  wire [31:0] adder_1_out, adder_2_out, adder_4_out, adder_5_out, C, C_prime, mux_1x32_1_o, mux_1x32_2_o,
       mux_1x32_3_o, mux_1x32_4_o, O_prime;

  MUX_1x32 mux_1x32_1 (.I1({in_2[31:1], 1'b0}), .O(mux_1x32_1_o), .I0({32{1'b0}}), .in_3(in_1[0]));
  Adder #(.width(32)) adder_1 (.a({O, 2'b00}), .b(mux_1x32_1_o), .out(adder_1_out), .cout(C1));  // open: cin
  MUX_1x32 mux_1x32_2 (.I1({in_1[31:1], 1'b0}), .O(mux_1x32_2_o), .I0({32{1'b0}}), .in_3(in_2[0]));
  Adder #(.width(32)) adder_2 (.a(adder_1_out), .b(mux_1x32_2_o), .out(adder_2_out), .cout(C2));  // open: cin
  and and_1 (and_1_out, in_1[0], in_2[0]);
  Adder #(.width(32)) adder_3 (.a(adder_2_out), .b({32{1'b0}}), .out(O_prime), .cin(and_1_out), .cout(C3));
  MUX_1x32 mux_1x32_3 (.I1(in_1), .O(mux_1x32_3_o), .I0({1'b0, in_1[31:1]}), .in_3(in_3));
  MUX_1x32 mux_1x32_4 (.I1(in_2), .O(mux_1x32_4_o), .I0({1'b0, in_2[31:1]}), .in_3(in_3));
  MUX_1x32 mux_1x32_5 (.I1(C), .O(HIGHT), .I0(C_prime), .in_3(in_3));
  Adder #(.width(32)) adder_4 (.a({C[29:0], C_U}), .b({32{1'b0}}), .out(adder_4_out), .cin(C1));  // open: cout
  Multiplier #(.width(32)) multiplier_1 (.a(mux_1x32_3_o), .b(mux_1x32_4_o), .out({C_U, O}), .cout(C));  // open: cin
  Adder #(.width(32)) adder_5 (.a(adder_4_out), .b({32{1'b0}}), .out(adder_5_out), .cin(C2));  // open: cout
  MUX_1x32 mux_1x32_6 (.I1({C_U, O}), .O(LOW), .I0(O_prime), .in_3(in_3));
  Adder #(.width(32)) adder_6 (.a({32{1'b0}}), .b(adder_5_out), .out(C_prime), .cin(C2));  // open: cout

  // Other names for the same wires on the sheet: A[31:0] = in_1; A0 = in_1[0]; AP[31:1] = in_1[31:1];
  //   SR_A[30:0] = in_1[31:1]; B[31:0] = in_2; B0 = in_2[0]; BP[31:1] = in_2[31:1]; SR_B[30:0] = in_2[31:1];
  //   C_O[31:0] = HIGHT; C_U[31:2] = C[29:0]; O[31:30] = C_U; O_O[31:0] = LOW; O_U[31:2] = O; SIGN = in_3
endmodule

module DIV (
  input  [31:0] Dividend,
  input  [31:0] Divisor,
  input  in_3,
  output [31:0] Output,
  output [31:0] Remainder
);

  wire AC, BC, QC;
  wire [31:0] mux_1x32_1_o, mux_1x32_2_o, negator_1_out, negator_2_out, negator_3_out, negator_4_out, Q, R;

  xor xor_1 (QC, AC, BC);
  and and_1 (AC, Dividend[31], in_3);
  and and_2 (BC, in_3, Divisor[31]);
  Negator #(.width(32)) negator_1 (.in(Dividend), .out(negator_1_out));
  Negator #(.width(32)) negator_2 (.in(Divisor), .out(negator_2_out));
  MUX_1x32 mux_1x32_1 (.I1(negator_1_out), .O(mux_1x32_1_o), .I0(Dividend), .in_3(AC));
  MUX_1x32 mux_1x32_2 (.I1(negator_2_out), .O(mux_1x32_2_o), .I0(Divisor), .in_3(AC));
  Divider #(.width(32)) divider_1 (.a(mux_1x32_1_o), .b(mux_1x32_2_o), .out(Q), .rem(R));  // open: upper
  Negator #(.width(32)) negator_3 (.in(Q), .out(negator_3_out));
  Negator #(.width(32)) negator_4 (.in(R), .out(negator_4_out));
  MUX_1x32 mux_1x32_3 (.I1(negator_3_out), .O(Output), .I0(Q), .in_3(QC));
  MUX_1x32 mux_1x32_4 (.I1(negator_4_out), .O(Remainder), .I0(R), .in_3(AC));

  // Other names for the same wires on the sheet: A[31:0] = Dividend; B[31:0] = Divisor; Q_prime[31:0] = Output;
  //   R_prime[31:0] = Remainder; SIGN = in_3

  // Notes on the sheet:
  //   INPUTS
  //   OUTPUTS
endmodule

module Comparer (
  input  [31:0] A,
  input  [31:0] B,
  input  in_3,
  output out_4,
  output out_5,
  output out_6
);

  wire tunnel, tunnel_t, tunnel_t_t_t, tunnel_t_t_t_t;

  Comparator #(.width(32)) comparator_1 (.a(A), .b(B), .gt(tunnel_t_t_t), .eq(out_4), .lt(tunnel));
  Multiplexer #(.enable("false")) multiplexer_1 (.in0(tunnel_t_t_t_t), .in1(tunnel_t_t_t), .out(out_6), .sel(in_3));
  Comparator #(.width(32), .mode("unsigned")) comparator_2 (
    .a(A), .b(B), .gt(tunnel_t_t_t_t), .lt(tunnel_t));  // open: eq
  Multiplexer #(.enable("false")) multiplexer_2 (.in0(tunnel_t), .in1(tunnel), .out(out_5), .sel(in_3));

  // Other names for the same wires on the sheet: less_than = out_5; more_than = out_6; SIGN = in_3;
  //   tunnel_t_t = out_4
endmodule

module PC (
  input  [31:0] PC_Input,
  input  Enable,
  input  Reset,
  input  CLOK,
  output [31:0] PC_Output
);

  Register #(.width(32)) PC (.D(PC_Input), .en(Enable), .Q(PC_Output), .clk(CLOK), .clr(Reset));
endmodule

// REGISTER FILE
module Register_File (
  input  in_1,
  input  [31:0] in_2,
  input  [4:0] in_3,
  input  in_4,
  input  [4:0] in_5,
  input  in_6,
  input  [4:0] in_7,
  input  in_8,
  input  [31:0] IHI,
  input  [31:0] ILO,
  input  in_11,
  input  [31:0] ISP,
  output [31:0] SA,
  output [31:0] SB,
  output [31:0] OHI,
  output [31:0] OLO,
  output [31:0] OSP
);

  wire L0, L1, L2, L3, L4, L5, L6, L7, L8, L9, L10, L11, L12, L13, L14, L15, L16, L17, L18, L19, L20, L21,
       L22, L23, L24, L25, L26, L27, L28, L29, L30;
  wire [31:0] I, O1, O2, O3, O4, O5, O6, O7, O8, O9, O10, O11, O12, O13, O14, O15, O16, O17, O18, O19, O20,
       O21, O22, O23, O24, O25, O26, O27, O28, O29, O30;

  MUX_1x32 mux_1x32_1 (.I1({32{1'b0}}), .O(I), .I0(in_2), .in_3(in_4));
  Register #(.width(32)) register_1 (.D(I), .en(L1), .Q(O1), .clk(in_1), .clr(in_4));
  Register #(.width(32)) register_2 (.D(I), .en(L2), .Q(O2), .clk(in_1), .clr(in_4));
  Register #(.width(32)) register_3 (.D(I), .en(L3), .Q(O3), .clk(in_1), .clr(in_4));
  Register #(.width(32)) register_4 (.D(I), .en(L4), .Q(O4), .clk(in_1), .clr(in_4));
  Register #(.width(32)) register_5 (.D(I), .en(L5), .Q(O5), .clk(in_1), .clr(in_4));
  Register #(.width(32)) register_6 (.D(I), .en(L6), .Q(O6), .clk(in_1), .clr(in_4));
  Register #(.width(32)) register_7 (.D(I), .en(L7), .Q(O7), .clk(in_1), .clr(in_4));
  Register #(.width(32)) register_8 (.D(I), .en(L8), .Q(O8), .clk(in_1), .clr(in_4));
  Register #(.width(32)) register_9 (.D(I), .en(L9), .Q(O9), .clk(in_1), .clr(in_4));
  Register #(.width(32)) register_10 (.D(I), .en(L10), .Q(O10), .clk(in_1), .clr(in_4));
  Register #(.width(32)) register_11 (.D(I), .en(L11), .Q(O11), .clk(in_1), .clr(in_4));
  Register #(.width(32)) register_12 (.D(I), .en(L12), .Q(O12), .clk(in_1), .clr(in_4));
  Register #(.width(32)) register_13 (.D(I), .en(L13), .Q(O13), .clk(in_1), .clr(in_4));
  Register #(.width(32)) register_14 (.D(I), .en(L14), .Q(O14), .clk(in_1), .clr(in_4));
  Register #(.width(32)) register_15 (.D(I), .en(L15), .Q(O15), .clk(in_1), .clr(in_4));
  Register #(.width(32)) register_16 (.D(ISP), .en(in_11), .Q(OSP), .clk(in_1), .clr(in_4));
  Register #(.width(32)) register_17 (.D(IHI), .en(in_8), .Q(OHI), .clk(in_1), .clr(in_4));
  Register #(.width(32)) register_18 (.D(ILO), .en(in_8), .Q(OLO), .clk(in_1), .clr(in_4));
  Register #(.width(32)) register_19 (.D(I), .en(L16), .Q(O16), .clk(in_1), .clr(in_4));
  Register #(.width(32)) register_20 (.D(I), .en(L17), .Q(O17), .clk(in_1), .clr(in_4));
  Register #(.width(32)) register_21 (.D(I), .en(L18), .Q(O18), .clk(in_1), .clr(in_4));
  Register #(.width(32)) register_22 (.D(I), .en(L19), .Q(O19), .clk(in_1), .clr(in_4));
  Register #(.width(32)) register_23 (.D(I), .en(L20), .Q(O20), .clk(in_1), .clr(in_4));
  Register #(.width(32)) register_24 (.D(I), .en(L21), .Q(O21), .clk(in_1), .clr(in_4));
  Register #(.width(32)) register_25 (.D(I), .en(L22), .Q(O22), .clk(in_1), .clr(in_4));
  Register #(.width(32)) register_26 (.D(I), .en(L23), .Q(O23), .clk(in_1), .clr(in_4));
  Register #(.width(32)) register_27 (.D(I), .en(L24), .Q(O24), .clk(in_1), .clr(in_4));
  Register #(.width(32)) register_28 (.D(I), .en(L25), .Q(O25), .clk(in_1), .clr(in_4));
  Register #(.width(32)) register_29 (.D(I), .en(L26), .Q(O26), .clk(in_1), .clr(in_4));
  Register #(.width(32)) register_30 (.D(I), .en(L27), .Q(O27), .clk(in_1), .clr(in_4));
  Register #(.width(32)) register_31 (.D(I), .en(L28), .Q(O28), .clk(in_1), .clr(in_4));
  Register #(.width(32)) register_32 (.D(I), .en(L29), .Q(O29), .clk(in_1), .clr(in_4));
  Register #(.width(32)) register_33 (.D(I), .en(L30), .Q(O30), .clk(in_1), .clr(in_4));
  Demultiplexer #(.select(5), .enable("false")) demultiplexer_1 (
    .out0(L0), .out1(L1), .out2(L2), .out3(L3), .out4(L4), .out5(L5), .out6(L6), .out7(L7), .out8(L8),
    .out9(L9), .out10(L10), .out11(L11), .out12(L12), .out13(L13), .out14(L14), .out15(L15), .out16(L16),
    .out17(L17), .out18(L18), .out19(L19), .out20(L20), .out21(L21), .out22(L22), .out23(L23), .out24(L24),
    .out25(L25), .out26(L26), .out27(L27), .out28(L28), .out29(L29), .out30(L30), .in(in_6), .sel(in_7));  // open: out31
  MUL_5x32 mul_5x32_1 (
    .I0({32{1'b0}}), .I1(O1), .I2(O2), .I3(O3), .I4(O4), .I5(O5), .I6(O6), .I7(O7), .I8(O8), .I9(O9),
    .I10(O10), .I11(O11), .I12(O12), .I13(O13), .I14(O14), .I15(O15), .I16(O16), .I17(O17), .I18(O18),
    .I19(O19), .I20(O20), .I21(O21), .I22(O22), .I23(O23), .I24(O24), .I25(O25), .I26(O26), .I27(O27),
    .I28(O28), .I29(O29), .I30(O30), .I31(OSP), .in_33(in_3), .out_34(SA));
  MUL_5x32 mul_5x32_2 (
    .I0({32{1'b0}}), .I1(O1), .I2(O2), .I3(O3), .I4(O4), .I5(O5), .I6(O6), .I7(O7), .I8(O8), .I9(O9),
    .I10(O10), .I11(O11), .I12(O12), .I13(O13), .I14(O14), .I15(O15), .I16(O16), .I17(O17), .I18(O18),
    .I19(O19), .I20(O20), .I21(O21), .I22(O22), .I23(O23), .I24(O24), .I25(O25), .I26(O26), .I27(O27),
    .I28(O28), .I29(O29), .I30(O30), .I31(OSP), .in_33(in_5), .out_34(SB));

  // Other names for the same wires on the sheet: CLK = in_1; ESP = in_11; M_D = in_8; R_W = in_6; RD[4:0] = in_7;
  //   Reset = in_4; RS[4:0] = in_3; RT[4:0] = in_5

  // Notes on the sheet:
  //   INPUTS
  //   OUTPUTS
  //   Register file
  //   Registers
  //   Selectors
endmodule

module Waiter (
  input  Enable,
  input  CLK,
  input  Reset,
  input  [3:0] Time,
  output End
);

  wire comparator_1_eq, comparator_1_gt, not_1_out, or_1_out;
  wire [3:0] counter_1_q, subtractor_1_out;

  or or_1 (or_1_out, comparator_1_gt, not_1_out, Reset);
  not not_1 (not_1_out, Enable);
  Counter #(.width(4), .max('hf)) counter_1 (
    .D(4'b0000), .count(Enable), .Q(counter_1_q), .clk(CLK), .clr(or_1_out));  // open: load, carry
  Comparator #(.width(4)) comparator_1 (
    .a(counter_1_q), .b(subtractor_1_out), .gt(comparator_1_gt), .eq(comparator_1_eq));  // open: lt
  D_Flip_Flop d_ff_1 (.clk(CLK), .D(comparator_1_eq), .Q(End), .reset(Reset));  // open: Qn, preset, en
  Subtractor #(.width(4)) subtractor_1 (.a(Time), .b(4'b0001), .out(subtractor_1_out));  // open: bin, bout
endmodule

module Let_Pass_Read (
  input  [31:0] in_1,
  output out_2
);

  wire and_1_out, and_2_out, not_1_out, S;

  not not_1 (not_1_out, in_1[28]);
  or or_1 (S, not_1_out, in_1[29]);
  and and_1 (and_1_out, ~in_1[5], ~in_1[4], ~in_1[3], ~in_1[2], ~in_1[1], ~in_1[0], ~S);  // AND_Gate
  and and_2 (and_2_out, in_1[26], in_1[27], ~in_1[28], ~in_1[29], ~in_1[30], in_1[31]);  // AND_Gate
  or or_2 (out_2, and_1_out, and_2_out);

  // Other names for the same wires on the sheet: _0 = in_1[0]; _1 = in_1[1]; _2 = in_1[2]; _3 = in_1[3]; _4 = in_1[4];
  //   _5 = in_1[5]; op0 = in_1[26]; op1 = in_1[27]; op2 = in_1[28]; op3 = in_1[29]; op4 = in_1[30]; op5 = in_1[31]
endmodule

module Let_Pass_Write (
  input  [31:0] in_1,
  output out_2
);

  wire and_1_out, and_2_out, not_1_out, S;

  not not_1 (not_1_out, in_1[28]);
  or or_1 (S, not_1_out, in_1[29]);
  and and_1 (and_1_out, ~in_1[5], ~in_1[4], ~in_1[3], ~in_1[2], ~in_1[1], in_1[0], ~S);  // AND_Gate
  and and_2 (and_2_out, in_1[26], in_1[27], ~in_1[28], in_1[29], ~in_1[30], in_1[31]);  // AND_Gate
  or or_2 (out_2, and_1_out, and_2_out);

  // Other names for the same wires on the sheet: _0 = in_1[0]; _1 = in_1[1]; _2 = in_1[2]; _3 = in_1[3]; _4 = in_1[4];
  //   _5 = in_1[5]; op0 = in_1[26]; op1 = in_1[27]; op2 = in_1[28]; op3 = in_1[29]; op4 = in_1[30]; op5 = in_1[31]
endmodule

module Instructions_I (
  input  [5:0] in_1,
  output ADDI,
  output ORI,
  output BEQ,
  output SLTI,
  output XORI,
  output BNE,
  output BLTZ,
  output SLTIU,
  output LW,
  output BLEZ,
  output ANDI,
  output SW,
  output BGTZ
);

  and and_1 (ADDI, ~in_1[5], ~in_1[4], in_1[3], ~in_1[2], ~in_1[1], ~in_1[0]);  // AND_Gate
  and and_2 (SLTI, ~in_1[5], ~in_1[4], in_1[3], ~in_1[2], in_1[1], ~in_1[0]);  // AND_Gate
  and and_3 (SLTIU, ~in_1[5], ~in_1[4], in_1[3], ~in_1[2], in_1[1], in_1[0]);  // AND_Gate
  and and_4 (ANDI, ~in_1[5], ~in_1[4], in_1[3], in_1[2], ~in_1[1], ~in_1[0]);  // AND_Gate
  and and_5 (ORI, ~in_1[5], ~in_1[4], in_1[3], in_1[2], ~in_1[1], in_1[0]);  // AND_Gate
  and and_6 (XORI, ~in_1[5], ~in_1[4], in_1[3], in_1[2], in_1[1], ~in_1[0]);  // AND_Gate
  and and_7 (LW, in_1[5], ~in_1[4], ~in_1[3], ~in_1[2], in_1[1], in_1[0]);  // AND_Gate
  and and_8 (SW, in_1[5], ~in_1[4], in_1[3], ~in_1[2], in_1[1], in_1[0]);  // AND_Gate
  and and_9 (BEQ, ~in_1[5], ~in_1[4], ~in_1[3], in_1[2], ~in_1[1], ~in_1[0]);  // AND_Gate
  and and_10 (BNE, ~in_1[5], ~in_1[4], ~in_1[3], in_1[2], ~in_1[1], in_1[0]);  // AND_Gate
  and and_11 (BLEZ, ~in_1[5], ~in_1[4], ~in_1[3], in_1[2], in_1[1], ~in_1[0]);  // AND_Gate
  and and_12 (BGTZ, ~in_1[5], ~in_1[4], ~in_1[3], in_1[2], in_1[1], in_1[0]);  // AND_Gate
  and and_13 (BLTZ, ~in_1[5], ~in_1[4], ~in_1[3], ~in_1[2], ~in_1[1], in_1[0]);  // AND_Gate

  // Other names for the same wires on the sheet: _0 = in_1[0]; Op_Code[5:0] = in_1; _1 = in_1[1]; _2 = in_1[2];
  //   _3 = in_1[3]; _4 = in_1[4]; _5 = in_1[5]
endmodule

module Inmediate_I (
  input  [15:0] in_1,
  input  [5:0] in_2,
  input  [31:0] in_3,
  output [31:0] out_4
);

  wire comparator_1_lt, comparator_2_lt;
  wire [31:0] I032, I32, RADDI, RANDI, RORI, RSLTI, RSLTIU, RXORI;

  Adder #(.width(32)) adder_1 (.a(in_3), .b(I32), .out(RADDI));  // open: cin, cout
  Comparator #(.width(32)) comparator_1 (.a(in_3), .b(I32), .lt(comparator_1_lt));  // open: gt, eq
  Comparator #(.width(32), .mode("unsigned")) comparator_2 (.a(in_3), .b(I32), .lt(comparator_2_lt));  // open: gt, eq
  assign RANDI = in_3 & I032;  // AND_Gate and_1, 32 bits wide
  assign RORI = in_3 | I032;  // OR_Gate or_1, 32 bits wide
  assign RXORI = in_3 ^ I032;  // XOR_Gate xor_1, 32 bits wide
  assign RSLTI = {{31{1'b0}}, comparator_1_lt};  // Bit_Extender bit_extender_1
  assign RSLTIU = {{31{1'b0}}, comparator_2_lt};  // Bit_Extender bit_extender_2
  assign I32 = {{16{in_1[15]}}, in_1};  // Bit_Extender bit_extender_3
  assign I032 = {{16{1'b0}}, in_1};  // Bit_Extender bit_extender_4
  MUX_3x32 mux_3x32_1 (
    .I0(RADDI), .I2(RSLTI), .I3(RSLTIU), .I4(RANDI), .I5(RORI), .I6(RXORI), .in_9(in_2[2:0]), .out_10(out_4));  // open: I1, I7

  // Other names for the same wires on the sheet: _0 = in_2[0]; Op_Code[5:0] = in_2; _1 = in_2[1]; _2 = in_2[2];
  //   A[31:0] = in_3; I015[15:0] = in_1; K[15:0] = in_1; I15 = in_1[15]; _3 = in_2[3]; _4 = in_2[4]; _5 = in_2[5];
  //   R[31:0] = out_4
endmodule

module Instructions_R (
  input  [5:0] in_1,
  input  [5:0] in_2,
  output NOP,
  output MULU,
  output SLTU,
  output XOR,
  output ADD,
  output DIV,
  output AND,
  output POP,
  output RND,
  output SUB,
  output DIVU,
  output OR,
  output PUSH,
  output KBD,
  output MUL,
  output SLT,
  output NOR,
  output JR,
  output MFHI,
  output MFLO,
  output HALT,
  output TTY
);

  wire and_24_out, and_25_out, N, not_1_out, S, T;

  and and_1 (NOP, ~in_1[5], ~in_1[4], ~in_1[3], ~in_1[2], ~in_1[1], ~in_1[0], N);  // AND_Gate
  and and_2 (ADD, in_1[5], ~in_1[4], ~in_1[3], ~in_1[2], ~in_1[1], ~in_1[0]);  // AND_Gate
  and and_3 (SUB, in_1[5], ~in_1[4], ~in_1[3], ~in_1[2], in_1[1], ~in_1[0]);  // AND_Gate
  and and_4 (MUL, ~in_1[5], in_1[4], in_1[3], ~in_1[2], ~in_1[1], ~in_1[0]);  // AND_Gate
  and and_5 (MFHI, ~in_1[5], in_1[4], ~in_1[3], ~in_1[2], ~in_1[1], ~in_1[0]);  // AND_Gate
  and and_6 (MULU, ~in_1[5], in_1[4], in_1[3], ~in_1[2], ~in_1[1], in_1[0]);  // AND_Gate
  and and_7 (DIV, ~in_1[5], in_1[4], in_1[3], ~in_1[2], in_1[1], ~in_1[0]);  // AND_Gate
  and and_8 (DIVU, ~in_1[5], in_1[4], in_1[3], ~in_1[2], in_1[1], in_1[0]);  // AND_Gate
  and and_9 (SLT, in_1[5], ~in_1[4], in_1[3], ~in_1[2], in_1[1], ~in_1[0]);  // AND_Gate
  and and_10 (MFLO, ~in_1[5], in_1[4], ~in_1[3], ~in_1[2], in_1[1], ~in_1[0]);  // AND_Gate
  and and_11 (SLTU, in_1[5], ~in_1[4], in_1[3], ~in_1[2], in_1[1], in_1[0]);  // AND_Gate
  and and_12 (AND, in_1[5], ~in_1[4], ~in_1[3], in_1[2], ~in_1[1], ~in_1[0]);  // AND_Gate
  and and_13 (OR, in_1[5], ~in_1[4], ~in_1[3], in_1[2], ~in_1[1], in_1[0]);  // AND_Gate
  and and_14 (NOR, in_1[5], ~in_1[4], ~in_1[3], in_1[2], in_1[1], in_1[0]);  // AND_Gate
  and and_15 (HALT, in_1[5], in_1[4], in_1[3], in_1[2], in_1[1], in_1[0]);
  and and_16 (T, in_2[0], in_2[3], in_2[5], in_2[4], in_2[2], in_2[1]);
  and and_17 (XOR, in_1[5], ~in_1[4], in_1[3], ~in_1[2], ~in_1[1], ~in_1[0]);  // AND_Gate
  and and_18 (POP, ~in_1[5], ~in_1[4], ~in_1[3], ~in_1[2], ~in_1[1], ~in_1[0], S);  // AND_Gate
  and and_19 (PUSH, ~in_1[5], ~in_1[4], ~in_1[3], ~in_1[2], ~in_1[1], in_1[0], S);  // AND_Gate
  and and_20 (JR, ~in_1[5], ~in_1[4], in_1[3], ~in_1[2], ~in_1[1], ~in_1[0]);  // AND_Gate
  and and_21 (TTY, ~in_1[5], ~in_1[4], ~in_1[3], ~in_1[2], ~in_1[1], in_1[0], T);  // AND_Gate
  nor nor_1 (N, in_2[0], in_2[3], in_2[5], in_2[4], in_2[2], in_2[1]);
  and and_22 (RND, ~in_1[5], ~in_1[4], ~in_1[3], ~in_1[2], in_1[1], ~in_1[0]);  // AND_Gate
  and and_23 (KBD, ~in_1[5], ~in_1[4], ~in_1[3], in_1[2], ~in_1[1], ~in_1[0]);  // AND_Gate
  and and_24 (and_24_out, in_2[5], in_2[4], in_2[3]);
  not not_1 (not_1_out, and_25_out);
  and and_25 (and_25_out, in_2[2], in_2[1], in_2[0]);
  and and_26 (S, and_24_out, not_1_out);

  // Other names for the same wires on the sheet: _0 = in_1[0]; F_Code[5:0] = in_1; _1 = in_1[1]; _2 = in_1[2];
  //   _3 = in_1[3]; _4 = in_1[4]; _5 = in_1[5]; o0 = in_2[0]; Op_Code[5:0] = in_2; o1 = in_2[1]; o2 = in_2[2];
  //   o3 = in_2[3]; o4 = in_2[4]; o5 = in_2[5]
endmodule

// R RAM
module Read_Ram (
  input  [31:0] RAMO0,
  input  [31:0] RAMO1,
  input  [31:0] I,
  input  [3:0] RT,
  input  in_5,
  input  [31:0] RAMO2,
  input  [31:0] RAMO3,
  input  CLK,
  input  in_9,
  input  Reset,
  input  EW,
  output END_Mode1,
  output [15:0] ADDR,
  output out_14,
  output [31:0] out_15,
  output END_Mode2
);

  wire END;

  MUX_2x32 mux_2x32_1 (.I0(RAMO0), .I1(RAMO1), .I2(RAMO2), .I3(RAMO3), .out_6(out_15), .in_5(I[3:2]));
  // Probe on I[3:2]
  Waiter waiter_1 (.CLK(CLK), .End(END), .Reset(Reset), .Enable(out_14), .Time(RT));
  D_Flip_Flop d_ff_1 (.clk(CLK), .D(EW), .Q(out_14), .en(1'b1), .reset(Reset));  // open: Qn, preset
  and and_1 (END_Mode1, END, in_5);
  and and_2 (END_Mode2, END, in_9);

  assign ADDR = I[19:4];

  // Other names for the same wires on the sheet: CS = out_14; OutputSelector[1:0] = I[3:2]; Address[15:0] = I[19:4];
  //   Mode1 = in_5; Mode2 = in_9; RAMOutpur2[31:0] = RAMO2; RAMOutput0[31:0] = RAMO0; RAMOutput1[31:0] = RAMO1;
  //   RAMOutput3[31:0] = RAMO3; Read[31:0] = out_15

  // Notes on the sheet:
  //   Inputs
  //   OUTPUTS
endmodule

// W RAM
module Write_RAM (
  input  [3:0] WT,
  input  [31:0] in_2,
  input  [31:0] InputValue,
  input  CLK,
  input  Reset,
  input  in_6,
  output [3:0] Mask,
  output [15:0] out_8,
  output out_9,
  output [31:0] out_10,
  output [31:0] out_11,
  output [31:0] out_12,
  output [31:0] out_13,
  output out_14
);

  Decoder #(.select(2), .enable("false")) decoder_1 (
    .out0(Mask[0]), .out1(Mask[1]), .out2(Mask[2]), .out3(Mask[3]), .sel(in_2[3:2]));
  MUX_1x32 mux_1x32_1 (.I1(InputValue), .O(out_10), .I0({32{1'b0}}), .in_3(Mask[0]));
  MUX_1x32 mux_1x32_2 (.I1(InputValue), .O(out_11), .I0({32{1'b0}}), .in_3(Mask[1]));
  MUX_1x32 mux_1x32_3 (.I1(InputValue), .O(out_12), .I0({32{1'b0}}), .in_3(Mask[2]));
  MUX_1x32 mux_1x32_4 (.I1(InputValue), .O(out_13), .I0({32{1'b0}}), .in_3(Mask[3]));
  Waiter waiter_1 (.CLK(CLK), .End(out_14), .Reset(Reset), .Enable(out_9), .Time(WT));
  D_Flip_Flop d_ff_1 (.clk(CLK), .D(in_6), .Q(out_9), .en(1'b1), .reset(Reset));  // open: Qn, preset

  assign out_8 = in_2[19:4];

  // Other names for the same wires on the sheet: CS = out_9; END = out_14; EW = in_6; InputSelector[1:0] = in_2[3:2];
  //   Address[15:0] = in_2[19:4]; S0 = Mask[0]; S1 = Mask[1]; S2 = Mask[2]; S3 = Mask[3]; RAMInput0[31:0] = out_10;
  //   RAMInput1[31:0] = out_11; RAMInput2[31:0] = out_12; RAMInput3[31:0] = out_13

  // Notes on the sheet:
  //   INPUTS
  //   OUTPUTS
endmodule

// ID
module Instructions_Decoder (
  input  [31:0] INS,
  output ADDI,
  output ORI,
  output BEQ,
  output SLTI,
  output XORI,
  output BNE,
  output BLTZ,
  output SLTIU,
  output LW,
  output BLEZ,
  output ANDI,
  output SW,
  output BGTZ,
  output II,
  output [4:0] out_16,
  output S,
  output NOP,
  output [4:0] out_19,
  output MULU,
  output IR,
  output [15:0] out_22,
  output [25:0] Address,
  output SLTU,
  output XOR,
  output [4:0] out_26,
  output [5:0] Code,
  output ADD,
  output DIV,
  output IJ,
  output AND,
  output POP,
  output RND,
  output SUB,
  output DIVU,
  output OR,
  output PUSH,
  output KBD,
  output MUL,
  output SLT,
  output NOR,
  output JR,
  output MFHI,
  output MFLO,
  output HALT,
  output TTY
);

  wire and_1_out, and_2_out, and_3_out, and_4_out, NI, not_1_out, not_2_out, not_3_out, not_4_out, not_5_out,
       not_6_out, not_7_out, not_8_out, not_9_out, not_10_out, not_11_out, or_3_out;
  wire [5:0] multiplexer_1_out, multiplexer_3_out, multiplexer_4_out;

  not not_1 (not_1_out, INS[30]);
  and and_1 (and_1_out, not_1_out, INS[26]);
  not not_2 (not_2_out, INS[30]);
  and and_2 (and_2_out, not_2_out, INS[28]);
  not not_3 (not_3_out, INS[30]);
  and and_3 (and_3_out, not_3_out, INS[29]);
  not not_4 (not_4_out, INS[29]);
  not not_5 (not_5_out, INS[28]);
  not not_6 (not_6_out, INS[27]);
  not not_7 (not_7_out, INS[26]);
  not not_8 (not_8_out, INS[29]);
  not not_9 (not_9_out, INS[28]);
  not not_10 (not_10_out, INS[26]);
  or or_1 (II, and_1_out, and_2_out, and_3_out);
  and and_4 (and_4_out, not_4_out, not_5_out, not_6_out, not_7_out);
  or or_2 (IR, and_4_out, INS[30]);
  and and_5 (IJ, not_8_out, not_9_out, INS[27], not_10_out);
  Comparator #(.width(32), .mode("unsigned")) comparator_1 (.a(INS), .b(32'hfc000000), .eq(NI));  // open: gt, lt
  or or_3 (or_3_out, II, IJ);
  Multiplexer #(.width(6), .enable("false")) multiplexer_1 (
    .in0(INS[5:0]), .in1(INS[31:26]), .out(multiplexer_1_out), .sel(or_3_out));
  Multiplexer #(.width(6), .enable("false")) multiplexer_2 (
    .in0(multiplexer_1_out), .in1(6'b111000), .out(Code), .sel(NI));
  not not_11 (not_11_out, INS[28]);
  or or_4 (S, not_11_out, INS[29]);
  Multiplexer #(.width(6), .enable("false")) multiplexer_3 (
    .in0(6'b111000), .in1(Code), .out(multiplexer_3_out), .sel(II));
  Multiplexer #(.width(6), .enable("false")) multiplexer_4 (
    .in0(6'b111000), .in1(Code), .out(multiplexer_4_out), .sel(IR));
  Instructions_I instructions_i_1 (
    .in_1(multiplexer_3_out), .ADDI(ADDI), .ORI(ORI), .BEQ(BEQ), .SLTI(SLTI), .XORI(XORI), .BNE(BNE),
    .BLTZ(BLTZ), .SLTIU(SLTIU), .LW(LW), .BLEZ(BLEZ), .ANDI(ANDI), .SW(SW), .BGTZ(BGTZ));
  Instructions_R instructions_r_1 (
    .in_1(multiplexer_4_out), .in_2(INS[31:26]), .NOP(NOP), .MULU(MULU), .SLTU(SLTU), .XOR(XOR), .ADD(ADD),
    .DIV(DIV), .AND(AND), .POP(POP), .RND(RND), .SUB(SUB), .DIVU(DIVU), .OR(OR), .PUSH(PUSH), .KBD(KBD),
    .MUL(MUL), .SLT(SLT), .NOR(NOR), .JR(JR), .MFHI(MFHI), .MFLO(MFLO), .HALT(HALT), .TTY(TTY));

  assign Address = INS[25:0];
  assign out_16 = INS[25:21];
  assign out_19 = INS[20:16];
  assign out_22 = INS[15:0];
  assign out_26 = INS[15:11];

  // Other names for the same wires on the sheet: K[15:0] = INS[15:0]; RD[4:0] = INS[15:11]; RT[4:0] = INS[20:16];
  //   RS[4:0] = INS[25:21]; Op[5:0] = INS[31:26]; op0 = INS[26]; op1 = INS[27]; op2 = INS[28]; op3 = INS[29];
  //   op4 = INS[30]; op5 = INS[31]

  // Notes on the sheet:
  //   OUTPUTS
endmodule

module Instructions_Fetcher (
  input  Clock,
  input  Reset,
  input  [31:0] Input,
  input  Enable,
  output [31:0] Output
);

  Register #(.width(32)) register_1 (
    .D(Input), .en(Enable), .Q({Output[7:0], Output[15:8], Output[23:16], Output[31:24]}), .clk(Clock),
    .clr(Reset));

  // Other names for the same wires on the sheet: CLK = Clock

  // Notes on the sheet:
  //   INPUTS
endmodule

module Selector_Input (
  input  ALU,
  input  INM,
  input  DS,
  input  HI,
  input  LO,
  input  RND,
  input  KBD,
  output [2:0] out_8
);

  wire not_1_out, not_2_out, not_3_out, not_4_out, not_5_out, not_6_out, not_7_out, not_8_out, not_9_out,
       not_10_out, not_11_out, not_12_out;

  not not_1 (not_1_out, ALU);
  not not_2 (not_2_out, INM);
  not not_3 (not_3_out, DS);
  not not_4 (not_4_out, HI);
  not not_5 (not_5_out, ALU);
  not not_6 (not_6_out, INM);
  not not_7 (not_7_out, LO);
  not not_8 (not_8_out, RND);
  not not_9 (not_9_out, ALU);
  not not_10 (not_10_out, DS);
  not not_11 (not_11_out, LO);
  not not_12 (not_12_out, KBD);
  and and_1 (out_8[2], not_1_out, not_2_out, not_3_out, not_4_out);
  and and_2 (out_8[1], not_5_out, not_6_out, not_7_out, not_8_out);
  and and_3 (out_8[0], not_9_out, not_10_out, not_11_out, not_12_out);
endmodule

module Select_Read (
  input  Pop,
  input  Lw
);
endmodule

// BC
module Branch_Control (
  input  [31:0] in_1,
  input  [31:0] in_2,
  input  [15:0] in_3,
  input  [25:0] in_4,
  input  [31:0] in_5,
  input  in_6,
  input  in_7,
  input  in_8,
  input  in_9,
  input  in_10,
  input  in_11,
  input  in_12,
  output [31:0] out_13,
  output LoadPC
);

  wire _0, _0_t, _0_t_t, and_1_out, and_2_out, and_3_out, and_4_out, and_5_out, and_6_out, and_7_out, njr,
       not_3_out, or_1_out, or_4_out, S, tunnel, tunnel_t;
  wire [29:0] I30;
  wire [31:0] adder_2_out, controlled_buffer_3_out, PC2, subtractor_1_out, subtractor_2_out;

  // Probe on in_1
  or or_1 (or_1_out, _0, _0_t);
  Comparator #(.width(32)) comparator_1 (.a(in_1), .b(in_2), .eq(tunnel_t));  // open: gt, lt
  Comparator #(.width(32)) comparator_2 (.a(in_1), .b({32{1'b0}}), .gt(_0_t_t), .eq(_0_t), .lt(_0));
  and and_1 (and_1_out, in_8, tunnel_t);
  and and_2 (and_2_out, in_6, tunnel);
  and and_3 (and_3_out, in_12, or_1_out);
  and and_4 (and_4_out, _0_t_t, in_11);
  and and_5 (and_5_out, in_10, _0);
  not not_1 (tunnel, tunnel_t);
  or or_2 (LoadPC, S, in_7, in_9);
  or or_3 (S, and_1_out, and_2_out, and_3_out, and_4_out, and_5_out);
  Subtractor #(.width(32)) subtractor_1 (.a(in_1), .b(32'h4), .out(subtractor_1_out));  // open: bin, bout
  Subtractor #(.width(32)) subtractor_2 (
    .a({in_5[31:28], in_4, 2'b00}), .b(32'h4), .out(subtractor_2_out));  // open: bin, bout
  or or_4 (or_4_out, in_7, in_9);
  not not_2 (njr, or_4_out);
  Adder #(.width(32)) adder_1 (.a(in_5), .b(32'h4), .out(PC2));  // open: cin, cout
  Adder #(.width(32)) adder_2 (.a(PC2), .b({I30, 2'b00}), .out(adder_2_out));  // open: cin, cout
  assign out_13 = in_9 ? subtractor_1_out : 32'bz;  // Controlled_Buffer controlled_buffer_1
  assign out_13 = in_7 ? subtractor_2_out : 32'bz;  // Controlled_Buffer controlled_buffer_2
  assign I30 = {{14{in_3[15]}}, in_3};  // Bit_Extender bit_extender_1
  and and_6 (and_6_out, njr, S);
  assign controlled_buffer_3_out = and_6_out ? adder_2_out : 32'bz;  // Controlled_Buffer controlled_buffer_3
  // Probe on subtractor_1_out
  not not_3 (not_3_out, S);
  and and_7 (and_7_out, njr, not_3_out);
  assign out_13 = and_7_out ? PC2 : 32'bz;  // Controlled_Buffer controlled_buffer_4
  Subtractor #(.width(32)) subtractor_3 (.a(controlled_buffer_3_out), .b(32'h4), .out(out_13));  // open: bin, bout
  // Probe on {in_5[31:28], in_4, 2'b00}

  // Other names for the same wires on the sheet: beq = in_8; bgtz = in_11; blez = in_12; bltz = in_10; bne = in_6;
  //   I015[15:0] = in_3; K[15:0] = in_3; I15 = in_3[15]; I32[31:2] = I30; IJ[31:2] = {in_5[31:28], in_4};
  //   Jump[25:0] = in_4; PC[31:0] = in_5; jr = in_9; jump_t = in_7; PCOut[31:0] = out_13; Rs[31:0] = in_1;
  //   Rt[31:0] = in_2

  // Notes on the sheet:
  //   INPUTS
endmodule

// CU
module Control_Unit (
  input  in_1,
  input  in_2,
  input  in_3,
  input  in_4,
  input  in_5,
  input  in_6,
  input  in_7,
  input  in_8,
  input  in_9,
  input  in_10,
  input  in_11,
  input  in_12,
  input  in_13,
  output out_14,
  output out_15,
  output out_16,
  output out_17,
  output out_18,
  output out_19,
  output out_20,
  output out_21,
  output out_22,
  output out_23,
  output out_24,
  output out_25,
  output out_26,
  output out_27
);

  wire d_ff_1_q, d_ff_2_q, d_ff_3_q, demultiplexer_1_out0, demultiplexer_2_out0, demultiplexer_3_out0,
       demultiplexer_3_out1, demultiplexer_4_out0, demultiplexer_4_out1, demultiplexer_5_out0,
       demultiplexer_5_out1, demultiplexer_6_out1, demultiplexer_7_out1, IDLE_q, or_1_out, or_2_out,
       or_4_out, or_5_out, or_6_out, or_7_out, or_8_out, or_9_out, or_10_out;

  or or_1 (or_1_out, demultiplexer_1_out0, demultiplexer_7_out1);
  or or_2 (or_2_out, in_2, ~in_1);  // OR_Gate
  D_Flip_Flop IDLE (.clk(in_3), .D(or_1_out), .Q(IDLE_q), .preset(or_2_out));  // open: Qn, en, reset
  Demultiplexer #(.enable("false")) demultiplexer_1 (
    .out0(demultiplexer_1_out0), .out1(out_14), .in(IDLE_q), .sel(in_1));
  or or_3 (out_17, out_26, out_14);
  or or_4 (or_4_out, demultiplexer_2_out0, out_17);
  D_Flip_Flop ReadInst (.clk(in_3), .D(or_4_out), .Q(out_18));  // open: Qn, preset, en, reset
  Demultiplexer #(.enable("false")) demultiplexer_2 (
    .out0(demultiplexer_2_out0), .out1(out_19), .in(out_18), .sel(in_4));
  D_Flip_Flop d_ff_1 (.clk(in_3), .D(out_19), .Q(d_ff_1_q));  // open: Qn, preset, en, reset
  and and_1 (out_21, d_ff_1_q, in_5);
  Demultiplexer #(.enable("false")) demultiplexer_3 (
    .out0(demultiplexer_3_out0), .out1(demultiplexer_3_out1), .in(d_ff_1_q), .sel(or_5_out));
  or or_5 (or_5_out, in_6, in_7);
  or or_6 (or_6_out, demultiplexer_4_out0, demultiplexer_3_out1);
  D_Flip_Flop WaitRAM (.clk(in_3), .D(or_6_out), .Q(out_22));  // open: Qn, preset, en, reset
  Demultiplexer #(.enable("false")) demultiplexer_4 (
    .out0(demultiplexer_4_out0), .out1(demultiplexer_4_out1), .in(out_22), .sel(in_8));
  Demultiplexer #(.enable("false")) demultiplexer_5 (
    .out0(demultiplexer_5_out0), .out1(demultiplexer_5_out1), .in(or_7_out), .sel(or_8_out));
  or or_7 (or_7_out, demultiplexer_3_out0, demultiplexer_4_out1);
  or or_8 (or_8_out, in_9, in_10);
  and and_2 (out_23, in_9, demultiplexer_5_out1);
  and and_3 (out_24, in_10, demultiplexer_5_out1);
  and and_4 (out_25, in_11, demultiplexer_5_out1);
  or or_9 (or_9_out, demultiplexer_5_out0, demultiplexer_5_out1);
  D_Flip_Flop d_ff_2 (.clk(in_3), .D(or_9_out), .Q(d_ff_2_q));  // open: Qn, preset, en, reset
  Demultiplexer #(.enable("false")) demultiplexer_6 (
    .out0(out_26), .out1(demultiplexer_6_out1), .in(d_ff_2_q), .sel(in_13));
  or or_10 (or_10_out, out_27, demultiplexer_6_out1);
  D_Flip_Flop d_ff_3 (.clk(in_3), .D(or_10_out), .Q(d_ff_3_q));  // open: Qn, preset, en, reset
  Demultiplexer #(.enable("false")) demultiplexer_7 (
    .out0(out_27), .out1(demultiplexer_7_out1), .in(d_ff_3_q), .sel(in_2));

  assign out_15 = out_14;
  assign out_16 = out_14;
  assign out_20 = out_19;

  // Other names for the same wires on the sheet: CLK = in_3; CLR = in_2; CLRIF = out_17; CLRKBD = out_14;
  //   CLRPC = out_14; CLRRF = out_14; EndFetchMode1 = in_4; EndFetchMode2 = in_8; EPush = out_21; HALT = in_13;
  //   Hi_Lo = out_24; KBD = in_11; KBD_ENABLE = out_25; LPC = out_26; LInst = out_19; LRand = out_19; Push = in_5;
  //   R_RAM = in_6; R_W = in_9; R_W_Hi_LO = in_10; Register = out_23; START = in_1; StartFetchMode1 = out_18;
  //   StartFetchMode2 = out_22; STOP = out_27; TTY = in_12; W_RAM = in_7

  // Notes on the sheet:
  //   INPUTS
  //   OUTPUTS
endmodule
